// Logisim project SAP-1_Microcomputer_CSE331.circ as structural Verilog: 12 circuits, main circuit main
module main (
  input  CLR,
  output [3:0] LOW,
  output [3:0] HIGH,
  output [3:0] out_4,
  output [3:0] out_5
);

  wire CLK_out, controlled_buffer_1_out, controller_1_cp, controller_1_ea, controller_1_ep, controller_1_eu,
       controller_1_hlt, controller_1_nce, controller_1_ne1, controller_1_nl1, controller_1_nla,
       controller_1_nlb, controller_1_nlm, controller_1_nlo, controller_1_su, not_1_out, not_2_out,
       not_3_out, not_4_out, not_5_out, not_6_out, not_7_out, not_8_out;
  wire [3:0] mar_1_out;
  wire [7:0] adder_1_output, bit_extender_1_out, reg_1_output, reg_2_output, reg_4_output, xor_1_out;

  Clock CLK (.out(CLK_out));
  not not_1 (not_1_out, controller_1_nlm);
  not not_2 (not_2_out, controller_1_nl1);
  assign controlled_buffer_1_out = not_3_out ? CLK_out : 1'bz;  // Controlled_Buffer controlled_buffer_1
  Program_Counter program_counter_1 (
    .CP(controller_1_cp), .EP(controller_1_ep), .CLR(CLR), .CLK(controlled_buffer_1_out), .\output (LOW));
  not not_3 (not_3_out, controller_1_hlt);
  MAR mar_1 (.IN(LOW), .ENABLE(not_1_out), .CLEAR(controlled_buffer_1_out), .CLOCK(CLR), .OUT(mar_1_out));
  not not_4 (not_4_out, controller_1_nce);
  REG reg_1 (.INPUT({HIGH, LOW}), .ENABLE(not_2_out), .CLK(controlled_buffer_1_out), .CLR(CLR), .OUTPUT(reg_1_output));
  Controller controller_1 (
    .CLK(controlled_buffer_1_out), .I7(reg_1_output[7]), .I6(reg_1_output[6]), .I5(reg_1_output[5]),
    .I4(reg_1_output[4]), .CLR(CLR), .HLT(controller_1_hlt), .CP(controller_1_cp), .EP(controller_1_ep),
    .nLM(controller_1_nlm), .nCE(controller_1_nce), .nL1(controller_1_nl1), .nE1(controller_1_ne1),
    .nLA(controller_1_nla), .EA(controller_1_ea), .SU(controller_1_su), .EU(controller_1_eu),
    .nLB(controller_1_nlb), .nLO(controller_1_nlo));
  RAM #(.addrWidth(4)) ram_1 (.addr(mar_1_out), .data({HIGH, LOW}), .ld(not_4_out));  // open: sel, clk, clr
  assign LOW = not_5_out ? reg_1_output[3:0] : 4'bz;  // Controlled_Buffer controlled_buffer_2
  not not_5 (not_5_out, controller_1_ne1);
  assign {HIGH, LOW} = controller_1_ea ? reg_2_output : 8'bz;  // Controlled_Buffer controlled_buffer_3
  not not_6 (not_6_out, controller_1_nla);
  not not_7 (not_7_out, controller_1_nlo);
  REG reg_2 (.INPUT({HIGH, LOW}), .ENABLE(not_6_out), .CLK(controlled_buffer_1_out), .CLR(CLR), .OUTPUT(reg_2_output));
  assign {HIGH, LOW} = controller_1_eu ? adder_1_output : 8'bz;  // Controlled_Buffer controlled_buffer_4
  REG reg_3 (
    .INPUT({HIGH, LOW}), .ENABLE(not_7_out), .CLK(controlled_buffer_1_out), .CLR(CLR), .OUTPUT({out_4, out_5}));
  Adder adder_1 (.A(reg_2_output), .B(xor_1_out), .OUTPUT(adder_1_output), .Cin(controller_1_su));
  not not_8 (not_8_out, controller_1_nlb);
  REG reg_4 (.INPUT({HIGH, LOW}), .ENABLE(not_8_out), .CLK(controlled_buffer_1_out), .CLR(CLR), .OUTPUT(reg_4_output));
  assign xor_1_out = reg_4_output ^ bit_extender_1_out;  // XOR_Gate xor_1, 8 bits wide
  Hex_Digit_Display hex_digit_display_1 (.value(out_4));  // open: dp
  assign bit_extender_1_out = {{7{controller_1_su}}, controller_1_su};  // Bit_Extender bit_extender_1
  Hex_Digit_Display hex_digit_display_2 (.value(out_5));  // open: dp

  // Notes on the sheet:
  //   INPUT REG
  //   RAM
  //   ACCUMULATOR
  //   OUTPUT REG
  //   ALU
  //   B REGISTER
endmodule

module Decoder (
  input  I7,
  input  I6,
  input  I5,
  input  I4,
  output LDA,
  output ADD,
  output SUB,
  output OUT,
  output HLT
);

  wire and_1_out, and_2_out, and_3_out, and_4_out, and_5_out, not_1_out, not_2_out, not_3_out, not_4_out;

  not not_1 (not_1_out, I7);
  not not_2 (not_2_out, I6);
  not not_3 (not_3_out, I5);
  not not_4 (not_4_out, I4);
  and and_1 (and_1_out, not_1_out, not_2_out, not_3_out, not_4_out);
  and and_2 (and_2_out, not_1_out, not_2_out, not_3_out, I4);
  and and_3 (and_3_out, not_1_out, not_2_out, I5, not_4_out);
  and and_4 (and_4_out, I7, I6, I5, not_4_out);
  and and_5 (and_5_out, I7, I6, I5, I4);
  buf buffer_1 (LDA, and_1_out);
  buf buffer_2 (ADD, and_2_out);
  buf buffer_3 (SUB, and_3_out);
  buf buffer_4 (OUT, and_4_out);
  buf buffer_5 (HLT, and_5_out);

  // Notes on the sheet:
  //   DECODER
endmodule

module Address_Register (
  input  x3,
  input  x2,
  input  x1,
  input  x0,
  input  LOAD,
  input  Clear,
  input  Clock,
  output y3,
  output y2,
  output y1,
  output y0
);

  wire and_1_out, and_2_out, and_3_out, and_4_out, and_5_out, and_6_out, and_7_out, and_8_out, d_ff_1_q,
       d_ff_2_q, d_ff_3_q, d_ff_4_q, not_1_out, or_1_out, or_2_out, or_3_out, or_4_out;

  assign y3 = 1'b1 ? d_ff_1_q : 1'bz;  // Controlled_Buffer controlled_buffer_1
  and and_1 (and_1_out, d_ff_1_q, not_1_out);
  or or_1 (or_1_out, and_1_out, and_2_out);
  D_Flip_Flop d_ff_1 (.clk(Clock), .D(or_1_out), .Q(d_ff_1_q), .reset(Clear));  // open: Qn, preset, en
  and and_2 (and_2_out, x3, LOAD);
  assign y2 = 1'b1 ? d_ff_2_q : 1'bz;  // Controlled_Buffer controlled_buffer_2
  and and_3 (and_3_out, d_ff_2_q, not_1_out);
  D_Flip_Flop d_ff_2 (.clk(Clock), .D(or_2_out), .Q(d_ff_2_q), .reset(Clear));  // open: Qn, preset, en
  and and_4 (and_4_out, x2, LOAD);
  or or_2 (or_2_out, and_3_out, and_4_out);
  assign y1 = 1'b1 ? d_ff_3_q : 1'bz;  // Controlled_Buffer controlled_buffer_3
  and and_5 (and_5_out, d_ff_3_q, not_1_out);
  D_Flip_Flop d_ff_3 (.clk(Clock), .D(or_3_out), .Q(d_ff_3_q), .reset(Clear));  // open: Qn, preset, en
  and and_6 (and_6_out, x1, LOAD);
  or or_3 (or_3_out, and_5_out, and_6_out);
  assign y0 = 1'b1 ? d_ff_4_q : 1'bz;  // Controlled_Buffer controlled_buffer_4
  not not_1 (not_1_out, LOAD);
  and and_7 (and_7_out, d_ff_4_q, not_1_out);
  or or_4 (or_4_out, and_7_out, and_8_out);
  D_Flip_Flop d_ff_4 (.clk(Clock), .D(or_4_out), .Q(d_ff_4_q), .reset(Clear));  // open: Qn, preset, en
  and and_8 (and_8_out, x0, LOAD);

  // Notes on the sheet:
  //   ADDRESS REGISTER
  //   ENABLE
endmodule

module Ring_Counter (
  input  Clock,
  input  CLR,
  output T6,
  output T5,
  output T4,
  output T3,
  output T2,
  output T1
);

  wire j_k_ff_1_qn, j_k_ff_2_qn, j_k_ff_3_qn, j_k_ff_4_qn, j_k_ff_5_qn, j_k_ff_6_q, not_1_out;

  J_K_Flip_Flop j_k_ff_1 (
    .J(T5), .clk(not_1_out), .K(j_k_ff_2_qn), .Q(T6), .Qn(j_k_ff_1_qn), .reset(CLR));  // open: preset, en
  J_K_Flip_Flop j_k_ff_2 (
    .J(T4), .clk(not_1_out), .K(j_k_ff_3_qn), .Q(T5), .Qn(j_k_ff_2_qn), .reset(CLR));  // open: preset, en
  J_K_Flip_Flop j_k_ff_3 (
    .J(T3), .clk(not_1_out), .K(j_k_ff_4_qn), .Q(T4), .Qn(j_k_ff_3_qn), .reset(CLR));  // open: preset, en
  J_K_Flip_Flop j_k_ff_4 (
    .J(T2), .clk(not_1_out), .K(j_k_ff_5_qn), .Q(T3), .Qn(j_k_ff_4_qn), .reset(CLR));  // open: preset, en
  J_K_Flip_Flop j_k_ff_5 (
    .J(T1), .clk(not_1_out), .K(j_k_ff_6_q), .Q(T2), .Qn(j_k_ff_5_qn), .reset(CLR));  // open: preset, en
  not not_1 (not_1_out, Clock);
  J_K_Flip_Flop j_k_ff_6 (
    .J(j_k_ff_1_qn), .clk(not_1_out), .K(T6), .Q(j_k_ff_6_q), .Qn(T1), .reset(CLR));  // open: preset, en

  // Notes on the sheet:
  //   RING COUNTER
endmodule

module True_Complement (
  input  S0,
  input  B,
  input  S1,
  output Y
);

  wire and_1_out, and_2_out, not_1_out;

  not not_1 (not_1_out, B);
  and and_1 (and_1_out, S0, B);
  and and_2 (and_2_out, not_1_out, S1);
  or or_1 (Y, and_1_out, and_2_out);

  // Notes on the sheet:
  //   True Complement
endmodule

module Full_Adder (
  input  Digit_1,
  input  Digit_2,
  input  Carry_In,
  output S,
  output C
);

  wire and_1_out, and_2_out, xor_1_out;

  xor xor_1 (xor_1_out, Digit_1, Digit_2);
  and and_1 (and_1_out, Digit_1, Digit_2);
  xor xor_2 (S, xor_1_out, Carry_In);
  and and_2 (and_2_out, xor_1_out, Carry_In);
  or or_1 (C, and_2_out, and_1_out);

  // Notes on the sheet:
  //   FULL ADDER
endmodule

module Program_Counter (
  input  CP,
  input  EP,
  input  CLR,
  input  CLK,
  output [3:0] \output 
);

  wire j_k_ff_1_q, j_k_ff_2_q, j_k_ff_3_q, j_k_ff_4_q, not_1_out, not_2_out, not_3_out;

  not not_1 (not_1_out, j_k_ff_2_q);
  J_K_Flip_Flop j_k_ff_1 (.J(CP), .clk(not_1_out), .K(CP), .Q(j_k_ff_1_q), .preset(CLR));  // open: Qn, en, reset
  assign \output [3] = EP ? j_k_ff_1_q : 1'bz;  // Controlled_Buffer controlled_buffer_1
  not not_2 (not_2_out, j_k_ff_3_q);
  J_K_Flip_Flop j_k_ff_2 (.J(CP), .clk(not_2_out), .K(CP), .Q(j_k_ff_2_q), .preset(CLR));  // open: Qn, en, reset
  assign \output [2] = EP ? j_k_ff_2_q : 1'bz;  // Controlled_Buffer controlled_buffer_2
  not not_3 (not_3_out, j_k_ff_4_q);
  J_K_Flip_Flop j_k_ff_3 (.J(CP), .clk(not_3_out), .K(CP), .Q(j_k_ff_3_q), .preset(CLR));  // open: Qn, en, reset
  assign \output [1] = EP ? j_k_ff_3_q : 1'bz;  // Controlled_Buffer controlled_buffer_3
  J_K_Flip_Flop j_k_ff_4 (.J(CP), .clk(CLK), .K(CP), .Q(j_k_ff_4_q), .preset(CLR));  // open: Qn, en, reset
  assign \output [0] = EP ? j_k_ff_4_q : 1'bz;  // Controlled_Buffer controlled_buffer_4

  // Notes on the sheet:
  //   PROGRAM COUNTER
endmodule

module ALU (
  input  Cin,
  input  A0,
  input  B0,
  input  A1,
  input  B1,
  input  A2,
  input  B2,
  input  A3,
  input  B3,
  input  A4,
  input  B4,
  input  A5,
  input  B5,
  input  A6,
  input  B6,
  input  A7,
  input  B7,
  output F0,
  output F1,
  output F2,
  output F3,
  output F4,
  output F5,
  output F6,
  output F7,
  output C_out
);

  wire full_adder_1_c, full_adder_2_c, full_adder_3_c, full_adder_4_c, full_adder_5_c, full_adder_6_c,
       full_adder_7_c, true_complement_1_y, true_complement_2_y, true_complement_3_y, true_complement_4_y,
       true_complement_5_y, true_complement_6_y, true_complement_7_y, true_complement_8_y;

  True_Complement true_complement_1 (.S0(1'b1), .B(B0), .S1(1'b0), .Y(true_complement_1_y));
  True_Complement true_complement_2 (.S0(1'b1), .B(B1), .S1(1'b0), .Y(true_complement_2_y));
  True_Complement true_complement_3 (.S0(1'b1), .B(B2), .S1(1'b0), .Y(true_complement_3_y));
  True_Complement true_complement_4 (.S0(1'b1), .B(B3), .S1(1'b0), .Y(true_complement_4_y));
  True_Complement true_complement_5 (.S0(1'b1), .B(B4), .S1(1'b0), .Y(true_complement_5_y));
  True_Complement true_complement_6 (.S0(1'b1), .B(B5), .S1(1'b0), .Y(true_complement_6_y));
  True_Complement true_complement_7 (.S0(1'b1), .B(B6), .S1(1'b0), .Y(true_complement_7_y));
  True_Complement true_complement_8 (.S0(1'b1), .B(B7), .S1(1'b0), .Y(true_complement_8_y));
  Full_Adder full_adder_1 (.Digit_1(A0), .Digit_2(true_complement_1_y), .Carry_In(Cin), .S(F0), .C(full_adder_1_c));
  Full_Adder full_adder_2 (
    .Digit_1(A1), .Digit_2(true_complement_2_y), .Carry_In(full_adder_1_c), .S(F1), .C(full_adder_2_c));
  Full_Adder full_adder_3 (
    .Digit_1(A2), .Digit_2(true_complement_3_y), .Carry_In(full_adder_2_c), .S(F2), .C(full_adder_3_c));
  Full_Adder full_adder_4 (
    .Digit_1(A3), .Digit_2(true_complement_4_y), .Carry_In(full_adder_3_c), .S(F3), .C(full_adder_4_c));
  Full_Adder full_adder_5 (
    .Digit_1(A4), .Digit_2(true_complement_5_y), .Carry_In(full_adder_4_c), .S(F4), .C(full_adder_5_c));
  Full_Adder full_adder_6 (
    .Digit_1(A5), .Digit_2(true_complement_6_y), .Carry_In(full_adder_5_c), .S(F5), .C(full_adder_6_c));
  Full_Adder full_adder_7 (
    .Digit_1(A6), .Digit_2(true_complement_7_y), .Carry_In(full_adder_6_c), .S(F6), .C(full_adder_7_c));
  Full_Adder full_adder_8 (.Digit_1(A7), .Digit_2(true_complement_8_y), .Carry_In(full_adder_7_c), .S(F7), .C(C_out));

  // Notes on the sheet:
  //   LSB
  //   MSB
  //   S0
  //   S1
  //   ALU
  //   LSB
  //   MSB
endmodule

module Adder (
  input  Cin,
  input  [7:0] A,
  input  [7:0] B,
  output [7:0] OUTPUT
);

  ALU alu_1 (
    .Cin(Cin), .A0(A[0]), .B0(B[0]), .A1(A[1]), .B1(B[1]), .A2(A[2]), .B2(B[2]), .A3(A[3]), .B3(B[3]),
    .A4(A[4]), .B4(B[4]), .A5(A[5]), .B5(B[5]), .A6(A[6]), .B6(B[6]), .A7(A[7]), .B7(B[7]), .F0(OUTPUT[0]),
    .F1(OUTPUT[1]), .F2(OUTPUT[2]), .F3(OUTPUT[3]), .F4(OUTPUT[4]), .F5(OUTPUT[5]), .F6(OUTPUT[6]),
    .F7(OUTPUT[7]));  // open: C_out

  // Notes on the sheet:
  //   ADDER
endmodule

module MAR (
  input  [3:0] IN,
  input  ENABLE,
  input  CLEAR,
  input  CLOCK,
  output [3:0] OUT
);

  Address_Register address_register_1 (
    .Clear(CLOCK), .LOAD(ENABLE), .Clock(CLEAR), .y3(OUT[3]), .x3(IN[3]), .x2(IN[2]), .x1(IN[1]), .x0(IN[0]),
    .y2(OUT[2]), .y1(OUT[1]), .y0(OUT[0]));

  // Notes on the sheet:
  //   MAR
endmodule

module REG (
  input  [7:0] INPUT,
  input  ENABLE,
  input  CLK,
  input  CLR,
  output [7:0] OUTPUT
);

  MAR mar_1 (.IN(INPUT[3:0]), .ENABLE(ENABLE), .CLEAR(CLK), .CLOCK(CLR), .OUT(OUTPUT[3:0]));
  MAR mar_2 (.IN(INPUT[7:4]), .ENABLE(ENABLE), .CLEAR(CLK), .CLOCK(CLR), .OUT(OUTPUT[7:4]));

  // Notes on the sheet:
  //   REGISTER
endmodule

module Controller (
  input  CLK,
  input  CLR,
  input  I7,
  input  I6,
  input  I5,
  input  I4,
  output HLT,
  output CP,
  output EP,
  output nLM,
  output nCE,
  output nL1,
  output nE1,
  output nLA,
  output EA,
  output SU,
  output EU,
  output nLB,
  output nLO
);

  wire and_1_out, and_2_out, and_3_out, and_4_out, and_5_out, and_6_out, and_7_out, and_8_out, and_9_out,
       and_10_out, and_11_out, and_12_out, and_13_out, and_14_out, and_15_out, and_16_out, decoder_1_add,
       decoder_1_lda, decoder_1_out, decoder_1_sub, nand_1_out, nand_2_out, or_1_out, or_2_out, or_3_out,
       or_4_out, or_6_out, ring_counter_1_t3, ring_counter_1_t4, ring_counter_1_t5, ring_counter_1_t6;

  Decoder decoder_1 (
    .I6(I6), .I5(I5), .I4(I4), .LDA(decoder_1_lda), .ADD(decoder_1_add), .SUB(decoder_1_sub),
    .OUT(decoder_1_out), .HLT(HLT), .I7(I7));
  and and_1 (and_1_out, decoder_1_lda, ring_counter_1_t4);
  and and_2 (and_2_out, decoder_1_add, ring_counter_1_t4);
  or or_1 (or_1_out, EP, and_1_out, and_2_out, and_4_out);
  not not_1 (nLM, or_1_out);
  and and_3 (and_3_out, decoder_1_lda, ring_counter_1_t5);
  and and_4 (and_4_out, decoder_1_sub, ring_counter_1_t4);
  and and_5 (and_5_out, decoder_1_add, ring_counter_1_t5);
  or or_2 (or_2_out, ring_counter_1_t3, and_3_out, and_5_out, and_6_out);
  not not_2 (nCE, or_2_out);
  and and_6 (and_6_out, decoder_1_sub, ring_counter_1_t5);
  not not_3 (nL1, ring_counter_1_t3);
  and and_7 (and_7_out, decoder_1_add, ring_counter_1_t4);
  and and_8 (and_8_out, decoder_1_lda, ring_counter_1_t4);
  or or_3 (or_3_out, and_8_out, and_7_out, and_9_out);
  not not_4 (nE1, or_3_out);
  and and_9 (and_9_out, decoder_1_sub, ring_counter_1_t4);
  and and_10 (and_10_out, decoder_1_lda, ring_counter_1_t5);
  Ring_Counter ring_counter_1 (
    .Clock(CLK), .CLR(CLR), .T6(ring_counter_1_t6), .T5(ring_counter_1_t5), .T4(ring_counter_1_t4),
    .T3(ring_counter_1_t3), .T2(CP), .T1(EP));
  and and_11 (and_11_out, decoder_1_add, ring_counter_1_t6);
  and and_12 (and_12_out, decoder_1_sub, ring_counter_1_t6);
  or or_4 (or_4_out, and_10_out, and_11_out, and_12_out);
  not not_5 (nLA, or_4_out);
  nand nand_1 (nand_1_out, decoder_1_out, ring_counter_1_t4);
  not not_6 (EA, nand_1_out);
  nand nand_2 (nand_2_out, decoder_1_sub, ring_counter_1_t6);
  not not_7 (SU, nand_2_out);
  and and_13 (and_13_out, decoder_1_add, ring_counter_1_t6);
  and and_14 (and_14_out, decoder_1_sub, ring_counter_1_t6);
  or or_5 (EU, and_13_out, and_14_out);
  and and_15 (and_15_out, decoder_1_add, ring_counter_1_t5);
  and and_16 (and_16_out, decoder_1_sub, ring_counter_1_t5);
  or or_6 (or_6_out, and_15_out, and_16_out);
  not not_8 (nLB, or_6_out);
  nand nand_3 (nLO, ring_counter_1_t4, decoder_1_out);

  // Notes on the sheet:
  //   CONTROLLER
endmodule
